// Logisim project glips.circ as structural Verilog: 5 circuits, main circuit main
module main (
  input  ENABLE_DEBUG,
  input  [7:0] DEBUG_COORDS,
  input  ENABLE_TEST_INPUT,
  input  [31:0] TEST_INPUT
);

  wire and_1_out, button_1_out, comparator_1_eq, GLOBAL_CLOCK_out, uc_1_branch, uc_1_jump, uc_1_memtoreg,
       uc_1_memwrite, uc_1_regdst, uc_1_regwrite, uc_1_ulasrc;
  wire [2:0] uc_1_ulacontrol3;
  wire [3:0] multiplexer_2_out;
  wire [7:0] bit_extender_4_out, multiplexer_6_out;
  wire [31:0] adder_1_out, adder_2_out, bit_extender_1_out, bit_extender_2_out, bit_extender_3_out, INPUT,
       multiplexer_3_out, multiplexer_4_out, multiplexer_5_out, multiplexer_7_out, PC_q, ram_1_data,
       registers_1_r0_d, registers_1_r1_d, ROM, shifter_1_out, ula_1_ula_coord, ula_1_ula_out;

  Register #(.width(32)) PC (.D(adder_1_out), .Q(PC_q), .clk(GLOBAL_CLOCK_out), .clr(button_1_out));  // open: en
  Button button_1 (.out(button_1_out));
  Clock GLOBAL_CLOCK (.out(GLOBAL_CLOCK_out));
  ROM #(.dataWidth(32)) rom_1 (.addr(PC_q[7:0]), .data(ROM));  // open: sel
  Multiplexer #(.width(32), .enable("false")) multiplexer_1 (
    .in0(ROM), .in1(TEST_INPUT), .out(INPUT), .sel(ENABLE_TEST_INPUT));
  UC uc_1 (
    .I3(INPUT[31]), .MemToReg(uc_1_memtoreg), .I2(INPUT[30]), .MemWrite(uc_1_memwrite), .I1(INPUT[29]),
    .Branch(uc_1_branch), .I0(INPUT[28]), .ULAControl(uc_1_ulacontrol3[2]),
    .ULAControl2(uc_1_ulacontrol3[1]), .ULAControl3(uc_1_ulacontrol3[0]), .ULASrc(uc_1_ulasrc),
    .RegDst(uc_1_regdst), .RegWrite(uc_1_regwrite), .Jump(uc_1_jump));
  Multiplexer #(.width(4), .enable("false")) multiplexer_2 (
    .in0(INPUT[19:16]), .in1(INPUT[27:24]), .out(multiplexer_2_out), .sel(uc_1_regdst));
  assign bit_extender_1_out = {{6{1'b0}}, INPUT[25:0]};  // Bit_Extender bit_extender_1
  Registers registers_1 (
    .DATA_WRITE(multiplexer_7_out), .R0_D(registers_1_r0_d), .R0(INPUT[19:16]), .CLK(GLOBAL_CLOCK_out),
    .R1_D(registers_1_r1_d), .R1(INPUT[23:20]), .RESET(button_1_out), .RW(multiplexer_2_out),
    .RW_2(uc_1_regwrite));
  assign bit_extender_2_out = {{28{1'b0}}, PC_q[31:28]};  // Bit_Extender bit_extender_2
  Adder #(.width(32)) adder_1 (.a(multiplexer_5_out), .b(32'h1), .out(adder_1_out));  // open: cin, cout
  assign bit_extender_3_out = {{16{1'b0}}, INPUT[15:0]};  // Bit_Extender bit_extender_3
  Shifter #(.width(32)) shifter_1 (.in(bit_extender_2_out), .\dist (5'b11100), .out(shifter_1_out));
  Adder #(.width(32)) adder_2 (.a(shifter_1_out), .b(bit_extender_1_out), .out(adder_2_out));  // open: cin, cout
  ULA ula_1 (
    .DATA_0(registers_1_r0_d), .DATA_1(multiplexer_3_out), .ULA_OUT(ula_1_ula_out),
    .ULA_SELECT(uc_1_ulacontrol3), .ULA_Coord(ula_1_ula_coord));
  Multiplexer #(.width(32), .enable("false")) multiplexer_3 (
    .in0(registers_1_r1_d), .in1(bit_extender_3_out), .out(multiplexer_3_out), .sel(uc_1_ulasrc));
  Comparator #(.width(32)) comparator_1 (.a(32'h1), .b(ula_1_ula_out), .eq(comparator_1_eq));  // open: gt, lt
  and and_1 (and_1_out, uc_1_branch, comparator_1_eq);
  Multiplexer #(.width(32), .enable("false")) multiplexer_4 (
    .in0(PC_q), .in1(bit_extender_3_out), .out(multiplexer_4_out), .sel(and_1_out));
  Multiplexer #(.width(32), .enable("false")) multiplexer_5 (
    .in0(multiplexer_4_out), .in1(adder_2_out), .out(multiplexer_5_out), .sel(uc_1_jump));
  Bit_Extender #(.in_width(32), .out_width(8)) bit_extender_4 (.in(ula_1_ula_coord), .out(bit_extender_4_out));
  Multiplexer #(.width(8), .enable("false")) multiplexer_6 (
    .in0(bit_extender_4_out), .in1(DEBUG_COORDS), .out(multiplexer_6_out), .sel(ENABLE_DEBUG));
  RAM #(.dataWidth(32), .bus("separate")) ram_1 (
    .addr(multiplexer_6_out), .din(registers_1_r1_d), .data(ram_1_data), .str(uc_1_memwrite),
    .clk(GLOBAL_CLOCK_out), .ld(1'b1), .clr(button_1_out));  // open: sel
  Multiplexer #(.width(32), .enable("false")) multiplexer_7 (
    .in0(ula_1_ula_out), .in1(ram_1_data), .out(multiplexer_7_out), .sel(uc_1_memtoreg));

  // Other names for the same wires on the sheet: CHOOSE = ENABLE_TEST_INPUT; DEBUG = ENABLE_DEBUG;
  //   DEBUG_COORD[7:0] = DEBUG_COORDS; TESTE[31:0] = TEST_INPUT

  // Notes on the sheet:
  //   contents of rom_1 (hex, n*v repeats v):
  //   0 30040004 904c000d 300d0000 904d000b 510c0002 520d0000 1120000 3cd0000 40310000 100d0001 80000003
  //   100c0001 80000001 300c0000 904c001c 300d0000 904d001a 510c0002 520d0000 1120000 11010010 3cd0000
  //   13030003 40310000 1d0d0001 80000010 1c0c0001 8000000e 300c0000 904c0044 300d0000 904d003b 30060000
  //   300e0000 904e0034 510c0002 520e0000 1120000 0 23010000 0 510e0002 520d0000 1120000 11010010 0
  //   25010000 0 65530000 6650000 1e0e0001 80000022 570c0002 580d0000 7780000 17070020 40670000 1d0d0001
  //   8000001f 1c0c0001 8000001d
  //   Instruction
  //   Immediate
  //   Reg. 1
  //   Reg. 2
endmodule

module ULA (
  input  [2:0] ULA_SELECT,
  input  [31:0] DATA_0,
  input  [31:0] DATA_1,
  output [31:0] ULA_Coord,
  output [31:0] ULA_OUT
);

  wire comparator_1_eq;
  wire [4:0] bit_extender_1_out;
  wire [31:0] adder_1_out, bit_extender_2_out, multiplier_1_out, shifter_1_out;

  Bit_Extender #(.in_width(32), .out_width(5)) bit_extender_1 (.in(DATA_1), .out(bit_extender_1_out));
  Comparator #(.width(32)) comparator_1 (.a(DATA_0), .b(DATA_1), .eq(comparator_1_eq));  // open: gt, lt
  Adder #(.width(32)) adder_1 (.a(DATA_0), .b(DATA_1), .out(adder_1_out));  // open: cin, cout
  Shifter #(.width(32)) shifter_1 (.in(DATA_0), .\dist (bit_extender_1_out), .out(shifter_1_out));
  Multiplier #(.width(32)) multiplier_1 (.a(DATA_0), .b(DATA_1), .out(multiplier_1_out));  // open: cin, cout
  assign bit_extender_2_out = {{31{1'b0}}, comparator_1_eq};  // Bit_Extender bit_extender_2
  Multiplexer #(.select(3), .width(32)) multiplexer_1 (
    .in0(adder_1_out), .in1(multiplier_1_out), .in2(shifter_1_out), .in4(DATA_1), .in7(bit_extender_2_out),
    .out(ULA_OUT), .sel(ULA_SELECT));  // open: in3, in5, in6, en

  assign ULA_Coord = DATA_0;
endmodule

module Registers (
  input  [31:0] DATA_WRITE,
  input  [3:0] R0,
  input  CLK,
  input  [3:0] R1,
  input  RESET,
  input  [3:0] RW,
  input  RW_2,
  output [31:0] R0_D,
  output [31:0] R1_D
);

  wire demultiplexer_1_out0, demultiplexer_1_out1, demultiplexer_1_out2, demultiplexer_1_out3,
       demultiplexer_1_out4, demultiplexer_1_out5, demultiplexer_1_out6, demultiplexer_1_out7,
       demultiplexer_1_out8, demultiplexer_1_out9, demultiplexer_1_out10, demultiplexer_1_out11,
       demultiplexer_1_out12, demultiplexer_1_out13, demultiplexer_1_out14, demultiplexer_1_out15;
  wire [31:0] register_1_q, register_2_q, register_3_q, register_4_q, register_5_q, register_6_q,
       register_7_q, register_8_q, register_9_q, register_10_q, register_11_q, register_12_q, register_13_q,
       register_14_q, register_15_q, register_16_q;

  Register #(.width(32)) register_1 (.en(demultiplexer_1_out0), .Q(register_1_q), .clk(CLK), .clr(RESET));  // open: D
  Register #(.width(32)) register_2 (
    .D(DATA_WRITE), .en(demultiplexer_1_out1), .Q(register_2_q), .clk(CLK), .clr(RESET));
  Register #(.width(32)) register_3 (
    .D(DATA_WRITE), .en(demultiplexer_1_out2), .Q(register_3_q), .clk(CLK), .clr(RESET));
  Register #(.width(32)) register_4 (
    .D(DATA_WRITE), .en(demultiplexer_1_out3), .Q(register_4_q), .clk(CLK), .clr(RESET));
  Register #(.width(32)) register_5 (
    .D(DATA_WRITE), .en(demultiplexer_1_out4), .Q(register_5_q), .clk(CLK), .clr(RESET));
  Register #(.width(32)) register_6 (
    .D(DATA_WRITE), .en(demultiplexer_1_out5), .Q(register_6_q), .clk(CLK), .clr(RESET));
  Register #(.width(32)) register_7 (
    .D(DATA_WRITE), .en(demultiplexer_1_out6), .Q(register_7_q), .clk(CLK), .clr(RESET));
  Register #(.width(32)) register_8 (
    .D(DATA_WRITE), .en(demultiplexer_1_out7), .Q(register_8_q), .clk(CLK), .clr(RESET));
  Register #(.width(32)) register_9 (
    .D(DATA_WRITE), .en(demultiplexer_1_out8), .Q(register_9_q), .clk(CLK), .clr(RESET));
  Register #(.width(32)) register_10 (
    .D(DATA_WRITE), .en(demultiplexer_1_out9), .Q(register_10_q), .clk(CLK), .clr(RESET));
  Demultiplexer #(.select(4), .enable("false")) demultiplexer_1 (
    .out0(demultiplexer_1_out0), .out1(demultiplexer_1_out1), .out2(demultiplexer_1_out2),
    .out3(demultiplexer_1_out3), .out4(demultiplexer_1_out4), .out5(demultiplexer_1_out5),
    .out6(demultiplexer_1_out6), .out7(demultiplexer_1_out7), .out8(demultiplexer_1_out8),
    .out9(demultiplexer_1_out9), .out10(demultiplexer_1_out10), .out11(demultiplexer_1_out11),
    .out12(demultiplexer_1_out12), .out13(demultiplexer_1_out13), .out14(demultiplexer_1_out14),
    .out15(demultiplexer_1_out15), .in(RW_2), .sel(RW));
  Register #(.width(32)) register_11 (
    .D(DATA_WRITE), .en(demultiplexer_1_out10), .Q(register_11_q), .clk(CLK), .clr(RESET));
  Register #(.width(32)) register_12 (
    .D(DATA_WRITE), .en(demultiplexer_1_out11), .Q(register_12_q), .clk(CLK), .clr(RESET));
  Register #(.width(32)) register_13 (
    .D(DATA_WRITE), .en(demultiplexer_1_out12), .Q(register_13_q), .clk(CLK), .clr(RESET));
  Register #(.width(32)) register_14 (
    .D(DATA_WRITE), .en(demultiplexer_1_out13), .Q(register_14_q), .clk(CLK), .clr(RESET));
  Register #(.width(32)) register_15 (
    .D(DATA_WRITE), .en(demultiplexer_1_out14), .Q(register_15_q), .clk(CLK), .clr(RESET));
  Register #(.width(32)) register_16 (
    .D(DATA_WRITE), .en(demultiplexer_1_out15), .Q(register_16_q), .clk(CLK), .clr(RESET));
  Multiplexer #(.select(4), .width(32), .disabled(0), .enable("false")) multiplexer_1 (
    .in0(register_1_q), .in1(register_2_q), .in2(register_3_q), .in3(register_4_q), .in4(register_5_q),
    .in5(register_6_q), .in6(register_7_q), .in7(register_8_q), .in8(register_9_q), .in9(register_10_q),
    .in10(register_11_q), .in11(register_12_q), .in12(register_13_q), .in13(register_14_q),
    .in14(register_15_q), .in15(register_16_q), .out(R0_D), .sel(R0));
  Multiplexer #(.select(4), .width(32), .enable("false")) multiplexer_2 (
    .in0(register_1_q), .in1(register_2_q), .in2(register_3_q), .in3(register_4_q), .in4(register_5_q),
    .in5(register_6_q), .in6(register_7_q), .in7(register_8_q), .in8(register_9_q), .in9(register_10_q),
    .in10(register_11_q), .in11(register_12_q), .in12(register_13_q), .in13(register_14_q),
    .in14(register_15_q), .in15(register_16_q), .out(R1_D), .sel(R1));
endmodule

module UC (
  input  I3,
  input  I2,
  input  I1,
  input  I0,
  output MemToReg,
  output MemWrite,
  output Branch,
  output ULAControl,
  output ULAControl2,
  output ULAControl3,
  output ULASrc,
  output RegDst,
  output RegWrite,
  output Jump
);

  wire and_3_out, and_4_out, and_5_out, and_6_out, and_7_out, and_8_out, and_9_out, not_1_out, not_2_out,
       not_3_out, not_4_out, not_5_out, not_6_out, not_7_out, not_8_out, not_9_out, not_10_out, not_11_out,
       not_12_out, not_13_out, not_14_out, not_15_out, not_16_out;

  not not_1 (not_1_out, I2);
  and and_1 (MemToReg, not_1_out, I1, not_2_out);
  not not_2 (not_2_out, I0);
  not not_3 (not_3_out, I1);
  and and_2 (MemWrite, I2, not_3_out, not_4_out);
  not not_4 (not_4_out, I0);
  not not_5 (not_5_out, I2);
  and and_3 (and_3_out, not_5_out, I1, I0);
  and and_4 (and_4_out, I2, not_6_out, I0);
  not not_6 (not_6_out, I1);
  and and_5 (and_5_out, I2, I1, not_7_out);
  not not_7 (not_7_out, I0);
  not not_8 (not_8_out, I3);
  not not_9 (not_9_out, I2);
  and and_6 (and_6_out, not_8_out, not_9_out, I0);
  not not_10 (not_10_out, I3);
  and and_7 (and_7_out, not_10_out, not_11_out, I0);
  not not_11 (not_11_out, I1);
  not not_12 (not_12_out, I0);
  or or_1 (RegDst, not_12_out, I2);
  not not_13 (not_13_out, I3);
  and and_8 (and_8_out, not_13_out, not_14_out);
  not not_14 (not_14_out, I2);
  not not_15 (not_15_out, I3);
  and and_9 (and_9_out, not_15_out, I0);
  and and_10 (Jump, I3, not_16_out);
  not not_16 (not_16_out, I0);
  or or_2 (ULAControl, and_3_out, I3);
  or or_3 (ULAControl2, and_4_out, I3);
  or or_4 (ULAControl3, and_5_out, I3);
  or or_5 (ULASrc, and_6_out, and_7_out);
  or or_6 (RegWrite, and_8_out, and_9_out, I1);

  assign Branch = I3;
endmodule

module ADD_SUB_MULT (
  input  [31:0] DATA_0,
  input  [31:0] DATA_1,
  output [31:0] ADD,
  output [31:0] SUB,
  output [31:0] MULT
);

  Adder #(.width(32)) adder_1 (.a(DATA_0), .b(DATA_1), .out(ADD));  // open: cin, cout
  Subtractor #(.width(32)) subtractor_1 (.a(DATA_0), .b(DATA_1), .out(SUB));  // open: bin, bout
  Multiplier #(.width(32)) multiplier_1 (.a(DATA_1), .b(DATA_0), .out(MULT));  // open: cin, cout
endmodule
